# Fritzing sketch ArduFarmBot (saved by Fritzing 0.9.3b)
breadboards: 1

parts:
  Part2 = Arduino Nano (Rev3.0)
  U2 = mystery part, 3 pins [chip_label=LDR part_number="LIGHT SENSOR"]
  Part5 = Soil Moisture Sensor [part_number="SOIL MOISTURE"]
  J4 = Power Jack [part_number="POWER 5V" package=power_jack_smd]
  S1 = Round Pushbutton [part_number=PUMP]
  S2 = Round Pushbutton [part_number=LAMP]
  U7 = RELAY [part_number="PUMP RELAY" package=relay-g5q]
  U8 = RELAY [part_number="LAMP RELAY" package=relay-g5q]
  S3 = Round Pushbutton [part_number=SENSORES]
  Part6 = Soil Moisture Sensor [part_number="SOIL MOISTURE"]
  LED4 = LED - 5mm [color="Yellow (595nm)" package="5 mm [THT]"]
  R7 = Resistor [tolerance=±5% resistance=10k package=THT]
  RHT2 = Humidity and Temperature Sensor RHT03 [part_number="DHT22 TEMP/HUM"]
  U9 = ESP8266 WiFi Module [part_number=ESP8266]
  R8 = Resistor [tolerance=±5% resistance=1k package=THT]
  R9 = Resistor [tolerance=±5% resistance=2.2k package=THT]
  J5 = Power Jack [part_number="POWER 3.3V" package=power_jack_smd]
  LCD_20x4 = LCD screen  # not connected
  IIC3 = IIC Convterter [part_number="LCD 20 x 4" package=converter]

nets:
  GND: Part2.GND, Part2.D12/MISO, U2.pin1, J4.GND, S1.leg1, S2.leg1, U8.MAIN, S3.leg0, LED4.cathode, RHT2.GND_2, U9.GND, R9.Pin_0, J5.GND, IIC3.GND
  N1: Part2.D2, U9.TXD
  N2: Part2.D3, R8.Pin_1
  N3: Part2.D4, U9.CH_PD
  N4: Part2.D5, R7.Pin_0, RHT2.Data-signal
  N5: Part2.D8, U8.NO
  N6: Part2.D9, S2.leg0
  N7: Part2.D10, U7.NO
  N8: Part2.D11/MOSI, S1.leg0
  VCC: Part2.VIN, U2.pin2, J4.GNDBREAK, RHT2.Vcc, IIC3.Vcc
  N9: Part2.A5, IIC3.SCL
  N10: Part2.A4, IIC3.SDA
  N11: Part2.A2, Part5.SIG
  N12: Part2.A1, Part6.SIG
  N13: Part2.A0, U2.pin3
  N14: Part2.D13/SCK, LED4.anode
  VCC_2: Part5.VCC, Part6.VCC
  N15: U7.COIL2, U8.COIL2
  N16: U9.RXD, R9.Pin_1
  N17: U9.VCC, J5.GNDBREAK

custom parts:
  ESP8266 WiFi Module: Generic WiFi Module based on the ESP8266 with onboard PCB antenna and UART communications
  LCD screen: A standard character display, usually with 2x16 characters. Comes in many colors.
  IIC Convterter: Parallel to IIC Converter for HD44780 family LCDs
